# Fritzing sketch Fan scetch (saved by Fritzing 0.9.5d)
breadboards: 1

parts:
  WeMos_D1_Mini1 = WeMos D1 Mini
  DS1 = DS18B20 1-Wire Temperature Sensor [part_number=DS18B20]
  R2 = Resistor [tolerance=±5% resistance=4.7k package="0805 [SMD]"]
  F1 = Fan - 4 wire [package=THT]

nets:
  5V: WeMos_D1_Mini1.5V, DS1.VDD, R2.Pin_0, F1.Power
  N1: WeMos_D1_Mini1.D1, DS1.DQ, R2.Pin_1
  N2: WeMos_D1_Mini1.D6, F1.PWM
  N3: WeMos_D1_Mini1.D7, F1.Tach
  GND: WeMos_D1_Mini1.G, DS1.GND, F1.GND

notes:
  Fan wires are as wires colors,
  not as fan connectors

custom parts:
  Fan - 4 wire: Fan, 4 wire with tach.
